# Fritzing sketch 0-1-0_Montage_elec (saved by Fritzing 0.9.3b)

parts:
  Composant4 = Adafruit Proto Shield R3 [part_number="Adafruit #2077"]
  Composant5 = MicroSD Card Module
  R12 = Rotary Potentiometer (Large) [maximum_resistance=100kΩ package=THT]
  R13 = Rotary Potentiometer (Large) [maximum_resistance=100kΩ package=THT]
  R14 = Rotary Potentiometer (Large) [maximum_resistance=100kΩ package=THT]
  ZS-042_RTC2 = ZS-042 RTC Module
  S4 = H-Bridge with L298N
  M2 = DC Motor
  VCC2 = 4 x AAA Battery Mount
  S5 = Momentary Switch [package=ksa_sealed_tac_switch]
  S6 = Momentary Switch [package=ksa_sealed_tac_switch]
  R15 = Photocell (LDR) [package=THT]

nets:
  GND: Composant4.GND, Composant5.GND, R12.leg1, ZS-042_RTC2.GND, S4.GND, VCC2.-, S5.1, S6.1, R15.pin_1
  VCC: Composant4.A0, Composant4.D7, Composant4.D8, Composant4.1, Composant4.P$5, Composant4.P$6, Composant4.+5V, Composant5.VCC, R12.leg2, ZS-042_RTC2.VCC, S4.12V, S4.5V, S5.3, S6.3, R15.pin_0
  N1: Composant4.A1, R12.wiper
  N2: Composant4.A2, R13.wiper
  N3: Composant4.A3, R14.wiper
  N4: Composant4.A4, ZS-042_RTC2.SDA
  N5: Composant4.A5, ZS-042_RTC2.SCL
  N6: Composant4.D2, S4.IN2
  N7: Composant4.D3, S4.IN1
  N8: Composant4.D4, S4.ENA
  N9: Composant4.D10, Composant5.CS
  N10: Composant4.D11, Composant5.MOSI
  N11: Composant4.D12, Composant5.MISO
  N12: Composant4.D13, Composant5.SCK
  N13: Composant4.VIN, VCC2.+
  N14: S4.M1-01, M2.pin_2
  N15: S4.M1-02, M2.pin_1

custom parts:
  Adafruit Proto Shield R3: This prototyping shield is the best out there (well, we think so, at least), and now is even better with Version R3 - updated for the most compatibility with just about all the Arduinos! It works with UNO, Mega, Leonardo, NG, Diecimila, Duemilanove, and compatible Arduinos. Yun's and Arduino Ethernets have a chunky Ethernet jack that gets in the way of stacking, you can use the stacking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
  H-Bridge with L298N: h-bridge
