# Fritzing sketch Dev_Mot_et_RTC (saved by Fritzing 0.9.3b)
breadboards: 1

parts:
  Composant1 = Arduino Uno (Rev3)
  M1 = DC Motor
  S1 = H-Bridge with L298N
  ZS-042_RTC1 = ZS-042 RTC Module
  S2 = Pushbutton [package="[THT]"]
  R1 = Resistor [tolerance=±5% resistance=220 package=THT]
  R4 = Resistor [tolerance=±5% resistance=220 package=THT]
  R5 = Resistor [tolerance=±5% resistance=220 package=THT]
  S3 = Pushbutton [package="[THT]"]
  R6 = Resistor [tolerance=±5% resistance=220 package=THT]
  VCC2 = 4 x AAA Battery Mount

nets:
  N1: Composant1.A4/SDA, ZS-042_RTC1.SDA, R4.Pin_0
  N2: Composant1.A5/SCL, ZS-042_RTC1.SCL, R1.Pin_1
  N3: Composant1.D8, S3.Pin_3, S3.Pin_4, R6.Pin_0
  N4: Composant1.D2, S1.IN2
  N5: Composant1.D3_PWM, S1.IN1
  N6: Composant1.D4, S1.ENA
  N7: Composant1.D7, S2.Pin_1, S2.Pin_2, R5.Pin_1
  3V3: Composant1.3V3, ZS-042_RTC1.VCC, R1.Pin_0, R4.Pin_1
  5V: Composant1.5V, S1.5V, R5.Pin_0, R6.Pin_1
  GND: Composant1.GND, S1.GND, ZS-042_RTC1.GND, S2.Pin_3, S2.Pin_4, S3.Pin_1, S3.Pin_2, VCC2.-
  N8: M1.pin_1, S1.M1-02
  N9: M1.pin_2, S1.M1-01
  N10: S1.12V, VCC2.+

custom parts:
  H-Bridge with L298N: h-bridge
