# Fritzing sketch Dev_mot_rtc_photoR_pot (saved by Fritzing 0.9.3b)
breadboards: 1

parts:
  Composant1 = Arduino Uno (Rev3)
  ZS-042_RTC1 = ZS-042 RTC Module
  S2 = Pushbutton [package="[THT]"]
  R1 = Resistor [tolerance=±5% resistance=220 package=THT]
  R4 = Resistor [tolerance=±5% resistance=220 package=THT]
  R5 = Resistor [tolerance=±5% resistance=220 package=THT]
  S3 = Pushbutton [package="[THT]"]
  R6 = Resistor [tolerance=±5% resistance=220 package=THT]
  R7 = Photocell (LDR) [package=THT]
  R8 = Resistor [tolerance=±5% resistance=10k package=THT]
  R9 = Rotary Potentiometer (Large) [maximum_resistance=100kΩ package=THT]
  S1 = H-Bridge with L298N
  M1 = DC Motor
  R10 = Rotary Potentiometer (Large) [maximum_resistance=5kΩ package=THT]
  R11 = Rotary Potentiometer (Large) [maximum_resistance=5kΩ package=THT]
  VCC1 = 4 x AAA Battery Mount

nets:
  N1: Composant1.A0, R7.pin_1, R8.Pin_0
  N2: Composant1.A1, R9.wiper
  N3: Composant1.A2, R10.wiper
  N4: Composant1.A3, R11.wiper
  N5: Composant1.A4/SDA, ZS-042_RTC1.SDA, R4.Pin_0
  N6: Composant1.A5/SCL, ZS-042_RTC1.SCL, R1.Pin_1
  N7: Composant1.D8, S3.Pin_3, S3.Pin_4, R6.Pin_0
  N8: Composant1.D2, S1.IN2
  N9: Composant1.D3_PWM, S1.IN1
  N10: Composant1.D4, S1.ENA
  N11: Composant1.D7, S2.Pin_1, S2.Pin_2, R5.Pin_1
  3V3: Composant1.3V3, ZS-042_RTC1.VCC, R1.Pin_0, R4.Pin_1
  5V: Composant1.5V, R5.Pin_0, R6.Pin_1, R7.pin_0, S1.5V
  GND: Composant1.GND, ZS-042_RTC1.GND, S2.Pin_3, S2.Pin_4, S3.Pin_1, S3.Pin_2, R8.Pin_1, S1.GND, VCC1.-
  N12: R9.leg1, R11.leg1
  N13: R9.leg2, R11.leg2
  N14: S1.12V, VCC1.+
  N15: S1.M1-01, M1.pin_2
  N16: S1.M1-02, S1.ENA-5V, M1.pin_1

custom parts:
  H-Bridge with L298N: h-bridge
